# Fritzing sketch RoboFinder (saved by Fritzing 0.9.3b)
circuit board: 8.46667cm x 5.64444cm
breadboards: 1

parts:
  Componente3 = Arduino Mega 2560 (Rev3)
  CUI-enc1 = AMT103
  U1 = L298 [package=multiwatt15_6400bgheatsink]
  VCC2 = Battery
  VCC3 = Battery
  VCC1 = Battery
  M1 = DC Motor
  CUI-enc2 = AMT103
  M2 = DC Motor
  HC-SR04_Sensor_1 = HC-SR04 Ultrasonic Distance Sensor
  HC-SR04_Sensor_2 = HC-SR04 Ultrasonic Distance Sensor

nets:
  N1: Componente3.D19/RX1, CUI-enc1.A
  N2: Componente3.D18/TX1, CUI-enc1.B
  SCL Jetson Nano: Componente3.SCL
  SDA Jetson Nano: Componente3.SDA
  GND Jeston Nano: Componente3.GND, CUI-enc1.GND, U1.CSA, U1.GND, U1.CSB, VCC3.-, CUI-enc2.GND, HC-SR04_Sensor_1.ECHO, HC-SR04_Sensor_2.ECHO
  N3: Componente3.D13_PWM, U1.ENA
  N4: Componente3.D12_PWM, U1.ENB
  N5: Componente3.VIN, U1.VS, VCC1.+
  N6: Componente3.D2_PWM, CUI-enc2.B
  N7: Componente3.D3_PWM, CUI-enc2.A
  5V: Componente3.5V, CUI-enc1.5V, U1.VLS, CUI-enc2.5V
  N8: Componente3.D22, HC-SR04_Sensor_1.TRIG
  N9: Componente3.D23, HC-SR04_Sensor_1.GND
  N10: Componente3.D24, HC-SR04_Sensor_2.TRIG
  N11: Componente3.D25, HC-SR04_Sensor_2.GND
  N12: Componente3.D38, U1.IN1
  N13: Componente3.D39, U1.IN2
  N14: Componente3.D40, U1.IN3
  N15: Componente3.D41, U1.IN4
  N16: U1.OUT1, M1.pin_1
  N17: U1.OUT2, M1.pin_2
  N18: U1.OUT3, M2.pin_1
  N19: U1.OUT4, M2.pin_2
  N20: VCC2.-, VCC3.+
  N21: VCC2.+, VCC1.-
  VCC: HC-SR04_Sensor_1.VCC, HC-SR04_Sensor_2.VCC

notes:
  Robo Finder
  Jetson Nano
